// Logisim project Calculator.circ as structural Verilog: 6 circuits, main circuit main
module main (
  input  in_1,
  input  in_2
);

  wire _0, _1, _2, _3, _4, _5, _6, _7, _8, _9, a1, a2, a3, add, alu_1_overflow, and_1_out, and_2_out,
       and_3_out, and_5_out, and_6_out, and_7_out, arit, b1, b2, b3, backspace, c1, c2, c3, C_out, clear,
       clear_entry, d1, d2, d3, d_ff_2_q, d_ff_4_q, e1, e2, e3, f1, f2, f3, g1, g2, g3, MemNaN, MemOver,
       minus, MSB, multiplexer_4_out, NaN, nand_1_out, nor_2_out, not_1_out, not_2_out, not_4_out, not_5_out,
       not_6_out, not_7_out, not_8_out, not_9_out, not_10_out, not_11_out, not_12_out, not_13_out, or_2_out,
       or_3_out, or_4_out, or_5_out, or_6_out, or_7_out, or_8_out, overflow, ovf, ovfBCD, pop, push,
       push_counter_q, pushIn, REG_TOS;
  wire [3:0] dcm_to_binary_encoder_1_b0;
  wire [4:0] multiplexer_3_out;
  wire [4:4] ovf_32_out;
  wire [6:0] binary_to_bcd_to_7_segment_1_f1, binary_to_bcd_to_7_segment_1_f2,
       binary_to_bcd_to_7_segment_1_f3, controlled_buffer_2_out, controlled_buffer_3_out,
       controlled_buffer_5_out;
  wire [7:0] adder_1_out, multiplexer_1_out;
  wire [8:0] alu_1_output, controlled_buffer_7_out, controlled_buffer_8_out, divider_1_out,
       multiplexer_2_out, multiplexer_5_out, multiplexer_6_out, multiplier_1_out, outputREG, outputTOS;
  wire [23:0] Counter_q;

  _7_Segment_Display u_7_segment_display_1 (.g(MSB));  // open: f, a, b, e, d, c, dp
  or or_1 (clear, C_out, overflow, MemOver);
  Multiplexer #(.width(9)) multiplexer_1 (
    .in0(outputREG), .in1(outputTOS), .out({MSB, multiplexer_1_out}), .sel(REG_TOS));  // open: en
  _7_Segment_Display u_7_segment_display_2 (.g(g3), .f(f3), .a(a3), .b(b3), .e(e3), .d(d3), .c(c3));  // open: dp
  _7_Segment_Display u_7_segment_display_3 (.g(g2), .f(f2), .a(a2), .b(b2), .e(e2), .d(d2), .c(c2));  // open: dp
  Button u__8 (.out(_8));
  Button u__7 (.out(_7));
  Button u__4 (.out(_4));
  Button u__5 (.out(_5));
  Button u__1 (.out(_1));
  Button u__2 (.out(_2));
  Button u__0 (.out(_0));
  Button C (.out(C_out));
  _7_Segment_Display u_7_segment_display_4 (.g(g1), .f(f1), .a(a1), .b(b1), .e(e1), .d(d1), .c(c1));  // open: dp
  Button u__9 (.out(_9));
  Button u__6 (.out(_6));
  Button u__3 (.out(_3));
  Button CE (.out(clear_entry));
  Binary_to_BCD_to_7_segment binary_to_bcd_to_7_segment_1 (
    .MSB(MSB), .B7(multiplexer_1_out[7]), .B6(multiplexer_1_out[6]), .B5(multiplexer_1_out[5]),
    .B4(multiplexer_1_out[4]), .B3(multiplexer_1_out[3]), .B2(multiplexer_1_out[2]),
    .B1(multiplexer_1_out[1]), .LSB(multiplexer_1_out[0]), .f3(binary_to_bcd_to_7_segment_1_f3[0]),
    .g3(binary_to_bcd_to_7_segment_1_f3[1]), .a3(binary_to_bcd_to_7_segment_1_f3[2]),
    .b3_2(binary_to_bcd_to_7_segment_1_f3[3]), .c3(binary_to_bcd_to_7_segment_1_f3[4]),
    .d3(binary_to_bcd_to_7_segment_1_f3[5]), .e3(binary_to_bcd_to_7_segment_1_f3[6]),
    .f2(binary_to_bcd_to_7_segment_1_f2[0]), .g2(binary_to_bcd_to_7_segment_1_f2[1]),
    .a2(binary_to_bcd_to_7_segment_1_f2[2]), .b2_2(binary_to_bcd_to_7_segment_1_f2[3]),
    .c2(binary_to_bcd_to_7_segment_1_f2[4]), .d2(binary_to_bcd_to_7_segment_1_f2[5]),
    .e2(binary_to_bcd_to_7_segment_1_f2[6]), .f1(binary_to_bcd_to_7_segment_1_f1[0]),
    .g1(binary_to_bcd_to_7_segment_1_f1[1]), .a1(binary_to_bcd_to_7_segment_1_f1[2]),
    .b1_2(binary_to_bcd_to_7_segment_1_f1[3]), .c1(binary_to_bcd_to_7_segment_1_f1[4]),
    .d1(binary_to_bcd_to_7_segment_1_f1[5]), .e1(binary_to_bcd_to_7_segment_1_f1[6]));
  Button button (.out(minus));
  Button button_2 (.out(add));
  Button P (.out(push));
  Button button_3 (.out(backspace));
  and and_1 (and_1_out, binary_to_bcd_to_7_segment_1_f3[6], binary_to_bcd_to_7_segment_1_f3[5], binary_to_bcd_to_7_segment_1_f3[4], binary_to_bcd_to_7_segment_1_f3[3], binary_to_bcd_to_7_segment_1_f3[2], binary_to_bcd_to_7_segment_1_f3[0]);
  assign {e1, d1, c1, b1, a1, g1, f1} = not_2_out ? controlled_buffer_2_out : 7'bz;  // Controlled_Buffer controlled_buffer_1
  assign controlled_buffer_2_out = not_1_out ? binary_to_bcd_to_7_segment_1_f1 : 7'bz;  // Controlled_Buffer controlled_buffer_2
  not not_1 (not_1_out, NaN);
  not not_2 (not_2_out, or_2_out);
  or or_2 (or_2_out, push, pop);
  not not_3 (ovfBCD, and_1_out);
  and and_2 (and_2_out, binary_to_bcd_to_7_segment_1_f2[6], binary_to_bcd_to_7_segment_1_f2[5], binary_to_bcd_to_7_segment_1_f2[4], binary_to_bcd_to_7_segment_1_f2[3], binary_to_bcd_to_7_segment_1_f2[2], binary_to_bcd_to_7_segment_1_f2[0]);
  nand nand_1 (nand_1_out, and_2_out, and_1_out);
  assign controlled_buffer_3_out = nand_1_out ? binary_to_bcd_to_7_segment_1_f2 : 7'bz;  // Controlled_Buffer controlled_buffer_3
  not not_4 (not_4_out, and_1_out);
  assign {e3, d3, c3, b3, a3, g3, f3} = not_2_out ? controlled_buffer_5_out : 7'bz;  // Controlled_Buffer controlled_buffer_4
  assign controlled_buffer_5_out = not_4_out ? binary_to_bcd_to_7_segment_1_f3 : 7'bz;  // Controlled_Buffer controlled_buffer_5
  assign {e2, d2, c2, b2, a2, g2, f2} = not_2_out ? controlled_buffer_3_out : 7'bz;  // Controlled_Buffer controlled_buffer_6
  not not_5 (not_5_out, NaN);
  and and_3 (and_3_out, push, not_5_out);
  not not_6 (not_6_out, MemNaN);
  Multiplexer #(.width(9)) multiplexer_2 (
    .in0(outputREG), .in1(alu_1_output), .out(multiplexer_2_out), .sel(pop));  // open: en
  nor nor_1 (pushIn, pop, push);
  D_Flip_Flop #(.trigger("falling")) push_counter (
    .clk(and_3_out), .D(not_7_out), .Q(push_counter_q), .en(not_7_out), .reset(clear));  // open: Qn, preset
  not not_7 (not_7_out, push_counter_q);
  and and_4 (pop, not_6_out, or_3_out);
  or or_3 (or_3_out, add, minus);
  D_Flip_Flop d_ff_1 (.clk(minus), .D(minus), .Q(arit), .reset(and_5_out));  // open: Qn, preset, en
  and and_5 (and_5_out, not_6_out, add);
  Register #(.width(9)) Top_of_Stack (.D(multiplexer_2_out), .Q(outputTOS), .clk(pushIn), .clr(clear));  // open: en
  or ovf_32 (ovf_32_out[4], outputREG[5], outputREG[6], outputREG[7], outputREG[8]);
  DCM_to_binary_Encoder dcm_to_binary_encoder_1 (
    .n9(_9), .n8(_8), .n7(_7), .n6(_6), .n5(_5), .n4(_4), .n3(_3), .n2(_2), .n1(_1),
    .b3(dcm_to_binary_encoder_1_b0[3]), .b2(dcm_to_binary_encoder_1_b0[2]),
    .b1(dcm_to_binary_encoder_1_b0[1]), .b0(dcm_to_binary_encoder_1_b0[0]));
  ALU alu_1 (
    .A(controlled_buffer_8_out), .B(outputTOS), .art(arit), .\output (alu_1_output), .overflow(alu_1_overflow));
  not not_8 (not_8_out, pop);
  and and_6 (and_6_out, push, push_counter_q);
  Multiplexer #(.width(5)) multiplexer_3 (
    .in0(outputREG[4:0]), .in1({5{ovf_32_out[4]}}), .out(multiplexer_3_out), .sel(ovf_32_out[4]));  // open: en
  D_Flip_Flop d_ff_2 (.clk(pop), .D(pop), .Q(d_ff_2_q), .reset(multiplexer_4_out));  // open: Qn, preset, en
  not not_9 (not_9_out, d_ff_2_q);
  Multiplexer multiplexer_4 (.in0(not_8_out), .in1(and_6_out), .out(multiplexer_4_out), .sel(not_9_out));  // open: en
  Multiplier #(.width(9)) multiplier_1 (
    .a({4'b0000, multiplexer_3_out}), .b(9'ha), .out(multiplier_1_out));  // open: cin, cout
  Adder #(.width(9)) adder_1 (
    .a(multiplier_1_out), .b({{5{1'b0}}, dcm_to_binary_encoder_1_b0}), .out({ovf, adder_1_out}));  // open: cin, cout
  or or_4 (or_4_out, _0, _1, _2, _3, _4, _6, _5, _7, _8, _9);
  not not_10 (not_10_out, pop);
  D_Flip_Flop d_ff_3 (.clk(not_10_out), .D(alu_1_overflow), .Q(overflow), .reset(clear));  // open: Qn, preset, en
  Counter #(.width(24), .max('hffffff)) Counter (
    .load(d_ff_2_q), .count(1'b1), .Q(Counter_q), .clk(multiplexer_4_out), .clr(clear));  // open: D, carry
  Multiplexer #(.width(9)) multiplexer_5 (
    .in0({ovf, adder_1_out}), .in1(divider_1_out), .out(multiplexer_5_out), .sel(backspace));  // open: en
  Divider #(.width(9)) divider_1 (.a(outputREG), .b(9'ha), .out(divider_1_out));  // open: upper, rem
  not not_11 (not_11_out, clear);
  not not_12 (not_12_out, and_6_out);
  Multiplexer #(.width(9)) multiplexer_6 (
    .in0(outputREG), .in1(multiplexer_5_out), .out(multiplexer_6_out), .sel(or_5_out));  // open: en
  or or_5 (or_5_out, backspace, nor_2_out);
  nor nor_2 (nor_2_out, ovf, ovfBCD);
  or or_6 (or_6_out, backspace, or_4_out);
  D_Flip_Flop #(.trigger("falling")) BCD_NaN_checker (
    .clk(or_4_out), .D(not_11_out), .Qn(NaN), .reset(clear));  // open: Q, preset, en
  or or_7 (or_7_out, or_4_out, clear, clear_entry);
  assign controlled_buffer_7_out = not_13_out ? outputTOS : 9'bz;  // Controlled_Buffer controlled_buffer_7
  RAM #(.addrWidth(24), .dataWidth(9)) ram_1 (
    .addr(Counter_q), .data(controlled_buffer_7_out), .clk(not_12_out), .ld(pop), .clr(clear));  // open: sel
  not not_13 (not_13_out, pop);
  Comparator #(.width(24)) comparator_1 (.a(Counter_q), .b({24{1'b0}}), .eq(MemNaN));  // open: gt, lt
  Comparator #(.width(24)) comparator_2 (.a(Counter_q), .b({24{1'b1}}), .eq(MemOver));  // open: gt, lt
  Register #(.width(9), .trigger("falling")) Register (
    .D(multiplexer_6_out), .Q(outputREG), .clk(or_6_out), .clr(or_8_out));  // open: en
  or or_8 (or_8_out, clear, clear_entry, and_7_out);
  D_Flip_Flop REG_or_TOS (.clk(pop), .D(pop), .Q(REG_TOS), .reset(or_7_out));  // open: Qn, preset, en
  assign controlled_buffer_8_out = not_13_out ? {9{1'b0}} : 9'bz;  // Controlled_Buffer controlled_buffer_8
  assign controlled_buffer_8_out = pop ? controlled_buffer_7_out : 9'bz;  // Controlled_Buffer controlled_buffer_9
  D_Flip_Flop d_ff_4 (.clk(push), .D(push), .Q(d_ff_4_q), .reset(and_7_out));  // open: Qn, preset, en
  and and_7 (and_7_out, d_ff_4_q, pushIn);
endmodule

module Binary_to_BCD_to_7_segment (
  input  MSB,
  input  B7,
  input  B6,
  input  B5,
  input  B4,
  input  B3,
  input  B2,
  input  B1,
  input  LSB,
  output f3,
  output g3,
  output a3,
  output b3_2,
  output c3,
  output d3,
  output e3,
  output f2,
  output g2,
  output a2,
  output b2_2,
  output c2,
  output d2,
  output e2,
  output f1,
  output g1,
  output a1,
  output b1_2,
  output c1,
  output d1,
  output e1
);

  wire ic_74185_1_y1, ic_74185_1_y2, ic_74185_1_y3, ic_74185_1_y4, ic_74185_1_y5, ic_74185_1_y6,
       ic_74185_2_y1, ic_74185_2_y2, ic_74185_2_y3, ic_74185_2_y4, ic_74185_2_y5, ic_74185_3_y1,
       ic_74185_3_y2, ic_74185_3_y3, ic_74185_3_y4, ic_74185_3_y5;
  wire [7:0] multiplexer_1_out, negator_1_out;

  Multiplexer #(.width(8)) multiplexer_1 (
    .in0({B7, B6, B5, B4, B3, B2, B1, LSB}), .in1(negator_1_out), .out(multiplexer_1_out), .sel(MSB));  // open: en
  Negator negator_1 (.in({B7, B6, B5, B4, B3, B2, B1, LSB}), .out(negator_1_out));
  ic_74185 ic_74185_1 (
    .E(multiplexer_1_out[7]), .D(multiplexer_1_out[6]), .C(multiplexer_1_out[5]), .B(multiplexer_1_out[4]),
    .A(multiplexer_1_out[3]), .Y6(ic_74185_1_y6), .Y5(ic_74185_1_y5), .Y4(ic_74185_1_y4), .Y3(ic_74185_1_y3),
    .Y2(ic_74185_1_y2), .Y1(ic_74185_1_y1));  // open: Y8, Y7
  ic_74185 ic_74185_2 (
    .E(ic_74185_1_y3), .D(ic_74185_1_y2), .C(ic_74185_1_y1), .B(multiplexer_1_out[2]),
    .A(multiplexer_1_out[1]), .Y5(ic_74185_2_y5), .Y4(ic_74185_2_y4), .Y3(ic_74185_2_y3), .Y2(ic_74185_2_y2),
    .Y1(ic_74185_2_y1));  // open: Y8, Y7, Y6
  ic_74185 ic_74185_3 (
    .E(1'b0), .D(ic_74185_1_y6), .C(ic_74185_1_y5), .B(ic_74185_1_y4), .A(ic_74185_2_y5), .Y5(ic_74185_3_y5),
    .Y4(ic_74185_3_y4), .Y3(ic_74185_3_y3), .Y2(ic_74185_3_y2), .Y1(ic_74185_3_y1));  // open: Y8, Y7, Y6
  BCD_to_7_segment bcd_to_7_segment_1 (
    .b3(1'b0), .b2(1'b0), .b1(ic_74185_3_y5), .b0(ic_74185_3_y4), .f(f3), .g(g3), .a(a3), .b(b3_2), .c(c3),
    .d(d3), .e(e3));
  BCD_to_7_segment bcd_to_7_segment_2 (
    .b3(ic_74185_3_y3), .b2(ic_74185_3_y2), .b1(ic_74185_3_y1), .b0(ic_74185_2_y4), .f(f2), .g(g2), .a(a2),
    .b(b2_2), .c(c2), .d(d2), .e(e2));
  BCD_to_7_segment bcd_to_7_segment_3 (
    .b3(ic_74185_2_y3), .b2(ic_74185_2_y2), .b1(ic_74185_2_y1), .b0(multiplexer_1_out[0]), .f(f1), .g(g1),
    .a(a1), .b(b1_2), .c(c1), .d(d1), .e(e1));
endmodule

module ic_74185 (
  input  E,
  input  D,
  input  C,
  input  B,
  input  A,
  output Y8,
  output Y7,
  output Y6,
  output Y5,
  output Y4,
  output Y3,
  output Y2,
  output Y1
);

  wire and_1_out, and_2_out, and_3_out, and_4_out, and_5_out, and_6_out, and_7_out, and_8_out, and_9_out,
       and_10_out, and_11_out, and_12_out, and_13_out, and_14_out, and_15_out, and_16_out, and_17_out,
       and_18_out, and_19_out, and_20_out, and_21_out, and_22_out, and_23_out, and_24_out, and_25_out,
       and_26_out, and_27_out, and_28_out, and_29_out, and_30_out, and_31_out, and_32_out, and_33_out,
       and_34_out, and_35_out, and_36_out, and_37_out, and_38_out, not_1_out, not_2_out, not_3_out,
       not_4_out, not_5_out, not_6_out, not_7_out, not_8_out, not_9_out, not_10_out, not_11_out, not_12_out,
       not_13_out, not_14_out, not_15_out, not_16_out, not_17_out, not_18_out, not_19_out, not_20_out,
       not_21_out, not_22_out, not_23_out, not_24_out, not_25_out, not_26_out, not_27_out, not_28_out,
       not_29_out, not_30_out, not_31_out, not_32_out, not_33_out, not_34_out, not_35_out, not_36_out,
       not_37_out, not_38_out, not_39_out, not_40_out, not_41_out, not_42_out, not_43_out, not_44_out,
       not_45_out, not_46_out, not_47_out, not_48_out, not_49_out, not_50_out, not_51_out, not_52_out,
       not_53_out, not_54_out, not_55_out, not_56_out, not_57_out, not_58_out, not_59_out, not_60_out,
       not_61_out, not_62_out, not_63_out, not_64_out, not_65_out, not_66_out, not_67_out, not_68_out,
       not_69_out, not_70_out, not_71_out;

  and and_1 (and_1_out, E, C);
  and and_2 (and_2_out, E, D);
  not not_1 (not_1_out, E);
  not not_2 (not_2_out, E);
  not not_3 (not_3_out, D);
  not not_4 (not_4_out, C);
  not not_5 (not_5_out, E);
  not not_6 (not_6_out, D);
  not not_7 (not_7_out, E);
  not not_8 (not_8_out, D);
  not not_9 (not_9_out, E);
  not not_10 (not_10_out, E);
  not not_11 (not_11_out, C);
  not not_12 (not_12_out, B);
  not not_13 (not_13_out, D);
  not not_14 (not_14_out, C);
  not not_15 (not_15_out, C);
  not not_16 (not_16_out, C);
  not not_17 (not_17_out, B);
  not not_18 (not_18_out, E);
  not not_19 (not_19_out, D);
  not not_20 (not_20_out, B);
  not not_21 (not_21_out, A);
  not not_22 (not_22_out, E);
  not not_23 (not_23_out, C);
  not not_24 (not_24_out, B);
  not not_25 (not_25_out, E);
  not not_26 (not_26_out, A);
  not not_27 (not_27_out, D);
  not not_28 (not_28_out, C);
  not not_29 (not_29_out, C);
  not not_30 (not_30_out, B);
  not not_31 (not_31_out, A);
  not not_32 (not_32_out, B);
  not not_33 (not_33_out, D);
  not not_34 (not_34_out, C);
  not not_35 (not_35_out, A);
  not not_36 (not_36_out, E);
  not not_37 (not_37_out, D);
  not not_38 (not_38_out, E);
  not not_39 (not_39_out, B);
  not not_40 (not_40_out, A);
  not not_41 (not_41_out, E);
  not not_42 (not_42_out, B);
  not not_43 (not_43_out, B);
  not not_44 (not_44_out, A);
  not not_45 (not_45_out, D);
  not not_46 (not_46_out, C);
  not not_47 (not_47_out, B);
  not not_48 (not_48_out, D);
  not not_49 (not_49_out, C);
  not not_50 (not_50_out, E);
  not not_51 (not_51_out, D);
  not not_52 (not_52_out, C);
  not not_53 (not_53_out, E);
  not not_54 (not_54_out, C);
  not not_55 (not_55_out, E);
  not not_56 (not_56_out, D);
  not not_57 (not_57_out, A);
  not not_58 (not_58_out, E);
  not not_59 (not_59_out, C);
  not not_60 (not_60_out, B);
  not not_61 (not_61_out, A);
  not not_62 (not_62_out, E);
  not not_63 (not_63_out, B);
  not not_64 (not_64_out, D);
  not not_65 (not_65_out, C);
  not not_66 (not_66_out, A);
  not not_67 (not_67_out, C);
  not not_68 (not_68_out, A);
  not not_69 (not_69_out, D);
  not not_70 (not_70_out, B);
  not not_71 (not_71_out, A);
  or or_1 (Y6, and_1_out, and_2_out);
  and and_3 (and_3_out, not_1_out, D, B);
  and and_4 (and_4_out, not_2_out, D, C);
  and and_5 (and_5_out, D, C, B);
  and and_6 (and_6_out, E, not_3_out, not_4_out);
  and and_7 (and_7_out, not_5_out, not_6_out, C, A);
  and and_8 (and_8_out, not_7_out, not_8_out, C, B);
  and and_9 (and_9_out, not_9_out, C, B, A);
  and and_10 (and_10_out, not_10_out, D, not_11_out, not_12_out);
  and and_11 (and_11_out, E, not_13_out, not_14_out);
  and and_12 (and_12_out, E, not_15_out, A);
  and and_13 (and_13_out, E, not_16_out, B);
  and and_14 (and_14_out, E, D, C, not_17_out);
  and and_15 (and_15_out, not_18_out, not_19_out, C, not_20_out, not_21_out);
  and and_16 (and_16_out, not_22_out, D, not_23_out, not_24_out, A);
  and and_17 (and_17_out, not_25_out, D, C, B, not_26_out);
  and and_18 (and_18_out, E, not_27_out, not_28_out, B, A);
  and and_19 (and_19_out, E, D, not_29_out, not_30_out, not_31_out);
  and and_20 (and_20_out, E, D, C, not_32_out, A);
  and and_21 (and_21_out, not_33_out, not_34_out, B, not_35_out);
  and and_22 (and_22_out, not_36_out, not_37_out, B, A);
  and and_23 (and_23_out, not_38_out, D, not_39_out, not_40_out);
  and and_24 (and_24_out, not_41_out, D, C, not_42_out);
  and and_25 (and_25_out, D, C, not_43_out, not_44_out);
  and and_26 (and_26_out, E, not_45_out, not_46_out, not_47_out, A);
  and and_27 (and_27_out, E, not_48_out, C, B);
  and and_28 (and_28_out, E, D, not_49_out, B, A);
  and and_29 (and_29_out, not_50_out, not_51_out, not_52_out, A);
  and and_30 (and_30_out, not_53_out, not_54_out, B, A);
  and and_31 (and_31_out, not_55_out, not_56_out, C, B, not_57_out);
  and and_32 (and_32_out, not_58_out, D, not_59_out, not_60_out, not_61_out);
  and and_33 (and_33_out, not_62_out, D, C, not_63_out, A);
  and and_34 (and_34_out, E, not_64_out, not_65_out, not_66_out);
  and and_35 (and_35_out, E, not_67_out, B, not_68_out);
  and and_36 (and_36_out, E, not_69_out, C, A);
  and and_37 (and_37_out, E, C, B, A);
  and and_38 (and_38_out, E, D, C, not_70_out, not_71_out);
  or or_2 (Y5, and_3_out, and_4_out, and_5_out, and_6_out);
  or or_3 (Y4, and_7_out, and_8_out, and_9_out, and_10_out, and_11_out, and_12_out, and_13_out, and_14_out);
  or or_4 (Y3, and_15_out, and_16_out, and_17_out, and_18_out, and_19_out, and_20_out);
  or or_5 (Y2, and_21_out, and_22_out, and_23_out, and_24_out, and_25_out, and_26_out, and_27_out, and_28_out);
  or or_6 (Y1, and_29_out, and_30_out, and_31_out, and_32_out, and_33_out, and_34_out, and_35_out, and_36_out, and_37_out, and_38_out);

  assign Y7 = 1'b1;
  assign Y8 = 1'b1;
endmodule

module BCD_to_7_segment (
  input  b3,
  input  b2,
  input  b1,
  input  b0,
  output f,
  output g,
  output a,
  output b,
  output c,
  output d,
  output e
);

  wire and_1_out, and_2_out, and_3_out, and_4_out, and_5_out, and_6_out, and_7_out, and_8_out, and_9_out,
       and_10_out, and_11_out, and_12_out, and_13_out, and_14_out, and_15_out, and_16_out, not_1_out,
       not_2_out, not_3_out, not_4_out, not_5_out, not_6_out, not_7_out, not_8_out, not_9_out, not_10_out,
       not_11_out, not_12_out, not_13_out, not_14_out, not_15_out, not_16_out, not_17_out, not_18_out,
       not_19_out, not_20_out, not_21_out;

  not not_1 (not_1_out, b1);
  and and_1 (and_1_out, not_1_out, not_2_out);
  not not_2 (not_2_out, b0);
  and and_2 (and_2_out, b2, not_3_out);
  not not_3 (not_3_out, b1);
  and and_3 (and_3_out, b2, not_4_out);
  not not_4 (not_4_out, b0);
  not not_5 (not_5_out, b2);
  and and_4 (and_4_out, not_5_out, b1);
  and and_5 (and_5_out, b2, not_6_out);
  not not_6 (not_6_out, b1);
  and and_6 (and_6_out, b2, not_7_out);
  not not_7 (not_7_out, b0);
  not not_8 (not_8_out, b2);
  and and_7 (and_7_out, not_8_out, not_9_out);
  not not_9 (not_9_out, b0);
  and and_8 (and_8_out, b2, b0);
  not not_10 (not_10_out, b2);
  not not_11 (not_11_out, b1);
  and and_9 (and_9_out, not_11_out, not_12_out);
  not not_12 (not_12_out, b0);
  and and_10 (and_10_out, b1, b0);
  not not_13 (not_13_out, b1);
  or or_1 (c, not_13_out, b0, b2);
  not not_14 (not_14_out, b2);
  and and_11 (and_11_out, not_14_out, not_15_out);
  not not_15 (not_15_out, b0);
  not not_16 (not_16_out, b2);
  and and_12 (and_12_out, not_16_out, b1);
  and and_13 (and_13_out, b1, not_17_out);
  not not_17 (not_17_out, b0);
  not not_18 (not_18_out, b1);
  and and_14 (and_14_out, b2, not_18_out, b0);
  not not_19 (not_19_out, b2);
  and and_15 (and_15_out, not_19_out, not_20_out);
  not not_20 (not_20_out, b0);
  and and_16 (and_16_out, b1, not_21_out);
  not not_21 (not_21_out, b0);
  or or_2 (f, and_1_out, and_2_out, and_3_out, b3);
  or or_3 (g, and_4_out, and_5_out, and_6_out, b3);
  or or_4 (a, and_7_out, b1, and_8_out, b3);
  or or_5 (b, not_10_out, and_9_out, and_10_out);
  or or_6 (d, and_11_out, and_12_out, and_13_out, and_14_out);
  or or_7 (e, and_15_out, and_16_out);
endmodule

module DCM_to_binary_Encoder (
  input  n9,
  input  n8,
  input  n7,
  input  n6,
  input  n5,
  input  n4,
  input  n3,
  input  n2,
  input  n1,
  output b3,
  output b2,
  output b1,
  output b0
);

  or or_1 (b3, n8, n9);
  or or_2 (b2, n4, n5, n6, n7);
  or or_3 (b1, n2, n3, n6, n7);
  or or_4 (b0, n1, n3, n5, n7, n9);
endmodule

module ALU (
  input  [8:0] A,
  input  [8:0] B,
  input  art,
  output [8:0] \output ,
  output overflow
);

  wire not_1_out, not_2_out, overflow_2_out, overflow_out;
  wire [8:0] multiplexer_1_out, negator_1_out;
  wire [9:9] adder_1_out;

  Negator #(.width(9)) negator_1 (.in(B), .out(negator_1_out));
  Multiplexer #(.width(9)) multiplexer_1 (
    .in0(B), .in1(negator_1_out), .out(multiplexer_1_out), .sel(art));  // open: en
  Adder #(.width(10)) adder_1 (
    .a({1'b0, A}), .b({1'b0, multiplexer_1_out}), .out({adder_1_out[9], \output }));  // open: cin, cout
  not not_1 (not_1_out, A[8]);
  not not_2 (not_2_out, multiplexer_1_out[8]);
  and u_overflow (overflow_out, not_1_out, \output [8], not_2_out);
  and overflow_2 (overflow_2_out, A[8], adder_1_out[9], multiplexer_1_out[8]);
  or or_1 (overflow, overflow_out, overflow_2_out);

  // Notes on the sheet:
  //   0 = +
  //   1 = -
endmodule
